# Fritzing sketch insulaSchematic_1 (saved by Fritzing 0.9.3b)
breadboards: 1

parts:
  Part1 = Arduino Nano (Rev3.0)
  3-Axis_Accelerometer1 = 3-Axis Accelerometer Breakout - MMA8452Q
  R1 = Basic Flex Resistor
  R2 = Basic Flex Resistor
  R3 = Resistor [tolerance=±5% resistance=220 package="2010 [SMD]"]
  R4 = Resistor [tolerance=±5% resistance=220 package="2010 [SMD]"]
  R5 = Basic Flex Resistor
  R6 = Basic Flex Resistor
  R7 = Resistor [tolerance=±5% resistance=220 package="2010 [SMD]"]
  R8 = Resistor [tolerance=±5% resistance=220 package="2010 [SMD]"]
  Part2 = Bluetooth HC-05 Macho

nets:
  N1: Part1.D1/TX, Part2.TXD
  N2: Part1.D0/RX, Part2.RXD
  GND: Part1.GND, 3-Axis_Accelerometer1.GND, R1.pin_1, R2.pin_1, R5.pin_1, R6.pin_1, Part2.GND
  N3: Part1.5V, R3.Pin_1, R4.Pin_1, R7.Pin_1, R8.Pin_1
  N4: Part1.A5, 3-Axis_Accelerometer1.SCL
  N5: Part1.A4, 3-Axis_Accelerometer1.SDA
  N6: Part1.A3, R6.Pin_2, R8.Pin_0
  N7: Part1.A2, R5.Pin_2, R7.Pin_0
  N8: Part1.A1, R2.Pin_2, R4.Pin_0
  N9: Part1.A0, R1.Pin_2, R3.Pin_0
  3V3: Part1.3V3, 3-Axis_Accelerometer1.3.3V, Part2.VCC
